# Fritzing sketch trafic_light (saved by Fritzing 0.9.5d)
circuit board: 8.46667cm x 5.64444cm
breadboards: 1

parts:
  Mod1 = Raspberry Pi Pico
  yellow = LED - 3mm [color="Yellow (595nm)" package="3 mm [THT]"]
  green = LED - 3mm [color="Green (555nm)" package="3 mm [THT]"]
  R1 = Resistor [tolerance=±5% resistance=220 package=THT]
  R2 = Resistor [tolerance=±5% resistance=220 package=THT]
  R3 = Resistor [tolerance=±5% resistance=220 package=THT]
  red = smd LED [color="Red (633nm)" package="1206 [SMD]"]

nets:
  N1: Mod1.pin_3, Mod1.pin_8, Mod1.pin_13, Mod1.pin_18, Mod1.pin_23, Mod1.pin_28, Mod1.pin_33, Mod1.pin_38
  N2: Mod1.pin_17, R3.Pin_0
  N3: Mod1.pin_19, R2.Pin_0
  N4: Mod1.pin_20, R1.Pin_0
  N5: Mod1.pin_37, yellow.cathode, green.cathode, red.cathode
  N6: yellow.anode, R2.Pin_1
  N7: green.anode, R3.Pin_1
  N8: R1.Pin_1, red.anode

custom parts:
  Raspberry Pi Pico: Raspberry Pi Pico. Based around the RP2040 microcontroller the Pico is a low cost microcontroller device bringing Raspberry Pi quality, cost, and easy of use to the microcontroller space. Jan 2021, Split part in to two versions: tht (this one) and SMD. This one will drill holes for a .1 in header in pcb to allow plugging in the module as well as providing pads to solder the module to the top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

// code stored in the sketch: Traffic_Light.py.ino
import machine
import utime

red_led = machine.Pin(15,machine.Pin.OUT)
yellow_led = machine.Pin(14,machine.Pin.OUT)
green_led = machine.Pin(13,machine.Pin.OUT)

while True:
    red_led.value(1)
    utime.sleep(5)
    yellow_led.value(1)
    utime.sleep(2)
    red_led.value(0)
    yellow_led.value(0)
    green_led.value(1)
    utime.sleep(5)
    green_led.value(0)
    yellow_led.value(1)
    utime.sleep(3)
    yellow_led.value(0)
